# Fritzing sketch FUC9OG8IGQY9RVI (saved by Fritzing 0.9.2b)
breadboards: 1

parts:
  Part1 = Arduino Uno (Rev3) [part_number=MCP]
  IC1 = IC, DIP package, 14 pins [chip_label=MCP42100]
  R3 = Resistor [tolerance=±5% resistance=470 package=THT]
  LED4 = LED - 5mm [color="Green (555nm)" package="5 mm [THT]"]
  R4 = Resistor [tolerance=±5% resistance=470 package=THT]
  LED3 = LED - 5mm [color="Green (555nm)" package="5 mm [THT]"]
  R1 = Resistor [tolerance=±5% resistance=4.7k package=THT]
  R2 = Resistor [tolerance=±5% resistance=4.7k package=THT]

nets:
  N1: Part1.D8, IC1.pin11, R2.Pin_1
  N2: Part1.D9_PWM, IC1.pin12, R1.Pin_1
  N3: Part1.D10_PWM/SS, IC1.pin1
  N4: Part1.D11_PWM/MOSI, IC1.pin3
  N5: Part1.D13/SCK, IC1.pin2
  N6: Part1.5V, IC1.pin7
  N7: Part1.GND, IC1.pin4, IC1.pin5, LED3.cathode
  N8: IC1.pin6, R4.Pin_0
  N9: IC1.pin8, IC1.pin14
  N10: IC1.pin9, R3.Pin_0
  N11: IC1.pin10, LED4.cathode, R1.Pin_0, R2.Pin_0
  N12: R3.Pin_1, LED4.anode
  N13: R4.Pin_1, LED3.anode
